// Logisim project Logical_unit.ver.01.circ as structural Verilog: 1 circuit, main circuit main
module main (
  input  [7:0] in_1,
  input  [7:0] in_2,
  input  in_3,
  input  in_4,
  input  in_5,
  output [7:0] out_6
);

  wire and_9_out, and_10_out, and_11_out, not_1_out, not_2_out;
  wire [7:0] and_1_out, or_1_out, xor_1_out;

  and and_1 (and_1_out[0], in_1[0], in_2[0]);
  and and_2 (and_1_out[1], in_1[1], in_2[1]);
  and and_3 (and_1_out[2], in_1[2], in_2[2]);
  and and_4 (and_1_out[3], in_1[3], in_2[3]);
  and and_5 (and_1_out[4], in_1[4], in_2[4]);
  and and_6 (and_1_out[5], in_1[5], in_2[5]);
  and and_7 (and_1_out[6], in_1[6], in_2[6]);
  and and_8 (and_1_out[7], in_1[7], in_2[7]);
  assign out_6 = and_11_out ? and_1_out : 8'bz;  // Controlled_Buffer controlled_buffer_1
  xor xor_1 (xor_1_out[0], in_1[0], in_2[0]);
  xor xor_2 (xor_1_out[1], in_1[1], in_2[1]);
  xor xor_3 (xor_1_out[2], in_1[2], in_2[2]);
  xor xor_4 (xor_1_out[3], in_1[3], in_2[3]);
  xor xor_5 (xor_1_out[4], in_1[4], in_2[4]);
  xor xor_6 (xor_1_out[5], in_1[5], in_2[5]);
  xor xor_7 (xor_1_out[6], in_1[6], in_2[6]);
  xor xor_8 (xor_1_out[7], in_1[7], in_2[7]);
  assign out_6 = and_10_out ? xor_1_out : 8'bz;  // Controlled_Buffer controlled_buffer_2
  or or_1 (or_1_out[0], in_1[0], in_2[0]);
  or or_2 (or_1_out[1], in_1[1], in_2[1]);
  or or_3 (or_1_out[2], in_1[2], in_2[2]);
  or or_4 (or_1_out[3], in_1[3], in_2[3]);
  or or_5 (or_1_out[4], in_1[4], in_2[4]);
  or or_6 (or_1_out[5], in_1[5], in_2[5]);
  or or_7 (or_1_out[6], in_1[6], in_2[6]);
  or or_8 (or_1_out[7], in_1[7], in_2[7]);
  assign out_6 = and_9_out ? or_1_out : 8'bz;  // Controlled_Buffer controlled_buffer_3
  not not_1 (not_1_out, in_4);
  not not_2 (not_2_out, in_5);
  and and_9 (and_9_out, in_3, in_4, not_2_out);
  and and_10 (and_10_out, in_3, not_1_out, in_5);
  and and_11 (and_11_out, in_3, not_1_out, not_2_out);
endmodule
