// Logisim project ALU_unfinished_ver.01.circ as structural Verilog: 2 circuits, main circuit main
module main (
  input  Enable,
  input  Clock,
  input  Choose000,
  input  Choose100,
  input  Choose010,
  input  [7:0] Ain,
  input  [7:0] Bin,
  input  Carryout,
  output [7:0] Dataout,
  output Flag100,
  output Flag010,
  output Flag000,
  output Overflow,
  output [7:0] out_14
);

  wire and_1_out, and_2_out, and_3_out, and_4_out, and_5_out, and_6_out, and_7_out, and_8_out, and_9_out,
       and_10_out, and_11_out, and_12_out, and_13_out, and_14_out, and_15_out, and_16_out, and_17_out,
       and_18_out, and_19_out, and_20_out, and_21_out, and_22_out, and_23_out, and_24_out, and_25_out,
       and_26_out, and_27_out, and_28_out, and_45_out, and_46_out, and_47_out, controlled_buffer_1_out,
       nand_1_out, nand_2_out, nand_3_out, nand_4_out, nand_5_out, nand_6_out, nand_7_out, nand_8_out,
       nand_9_out, nand_10_out, nand_11_out, nand_12_out, nand_13_out, nand_14_out, nand_15_out, nand_16_out,
       not_1_out, not_2_out, not_3_out, not_4_out, not_6_out, not_7_out, not_8_out, or_1_out, or_2_out,
       or_3_out, or_4_out, or_5_out, or_6_out, or_7_out, or_8_out, or_9_out, or_10_out, or_11_out, or_12_out,
       or_13_out, or_14_out, or_15_out, or_16_out, or_17_out, or_18_out, or_19_out, or_20_out, or_21_out,
       or_22_out, or_23_out, or_24_out, or_25_out, or_26_out, or_27_out, or_28_out, or_29_out, or_30_out,
       xor_1_out;
  wire [7:0] and_29_out, and_37_out, controlled_buffer_2_out, d_ff_4_q, not_5_out, or_31_out, xor_3_out,
       xor_11_out;

  not not_1 (not_1_out, Choose100);
  and and_1 (and_1_out, or_1_out, or_2_out, or_3_out);
  or or_1 (or_1_out, not_1_out, Choose100);
  not not_2 (not_2_out, Choose010);
  xor xor_1 (xor_1_out, Choose010, Carryout);
  or or_2 (or_2_out, not_2_out, Choose010);
  or or_3 (or_3_out, not_3_out, Choose000);
  not not_3 (not_3_out, Choose000);
  not not_4 (not_4_out, Choose000);
  and and_2 (and_2_out, Choose000, xor_1_out);
  and and_3 (and_3_out, not_4_out, Choose010);
  and and_4 (and_4_out, not_5_out[0], not_5_out[1], not_5_out[2], not_5_out[3], not_5_out[4], not_5_out[5], not_5_out[6], not_5_out[7]);
  or or_4 (or_4_out, Ain[0], xor_3_out[0]);
  and and_5 (and_5_out, Ain[0], xor_3_out[0]);
  or or_5 (or_5_out, Ain[1], xor_3_out[1]);
  and and_6 (and_6_out, Ain[1], xor_3_out[1]);
  or or_6 (or_6_out, Ain[2], xor_3_out[2]);
  and and_7 (and_7_out, Ain[2], xor_3_out[2]);
  or or_7 (or_7_out, Ain[3], xor_3_out[3]);
  and and_8 (and_8_out, Ain[3], xor_3_out[3]);
  assign controlled_buffer_1_out = and_1_out ? and_4_out : 1'bz;  // Controlled_Buffer controlled_buffer_1
  nand nand_1 (nand_1_out, Ain[0], xor_3_out[0]);
  nand nand_2 (nand_2_out, Ain[1], xor_3_out[1]);
  nand nand_3 (nand_3_out, Ain[2], xor_3_out[2]);
  nand nand_4 (nand_4_out, Ain[3], xor_3_out[3]);
  or or_8 (or_8_out, Ain[4], xor_3_out[4]);
  nand nand_5 (nand_5_out, Ain[4], xor_3_out[4]);
  and and_9 (and_9_out, Ain[4], xor_3_out[4]);
  or or_9 (or_9_out, Ain[5], xor_3_out[5]);
  nand nand_6 (nand_6_out, Ain[5], xor_3_out[5]);
  and and_10 (and_10_out, Ain[5], xor_3_out[5]);
  or or_10 (or_10_out, Ain[6], xor_3_out[6]);
  nand nand_7 (nand_7_out, Ain[6], xor_3_out[6]);
  and and_11 (and_11_out, Ain[6], xor_3_out[6]);
  or or_11 (or_11_out, Ain[7], xor_3_out[7]);
  nand nand_8 (nand_8_out, Ain[7], xor_3_out[7]);
  and and_12 (and_12_out, Ain[7], xor_3_out[7]);
  D_Flip_Flop d_ff_1 (.D(and_29_out[7]), .clk(Clock), .Q(Flag100));  // open: Qn, preset, reset
  buf or_12 (or_12_out, controlled_buffer_1_out);  // OR_Gate
  or or_13 (or_13_out, and_2_out, and_3_out);
  and and_13 (and_13_out, or_4_out, nand_1_out);
  and and_14 (and_14_out, or_5_out, nand_2_out);
  and and_15 (and_15_out, or_6_out, nand_3_out);
  and and_16 (and_16_out, or_7_out, nand_4_out);
  and and_17 (and_17_out, or_8_out, nand_5_out);
  and and_18 (and_18_out, or_9_out, nand_6_out);
  and and_19 (and_19_out, or_10_out, nand_7_out);
  and and_20 (and_20_out, or_11_out, nand_8_out);
  or or_14 (or_14_out, and_13_out, or_13_out);
  nand nand_9 (nand_9_out, and_13_out, or_13_out);
  and and_21 (and_21_out, and_13_out, or_13_out);
  or or_15 (or_15_out, or_22_out, and_14_out);
  nand nand_10 (nand_10_out, or_22_out, and_14_out);
  and and_22 (and_22_out, or_22_out, and_14_out);
  or or_16 (or_16_out, or_23_out, and_15_out);
  nand nand_11 (nand_11_out, or_23_out, and_15_out);
  and and_23 (and_23_out, or_23_out, and_15_out);
  or or_17 (or_17_out, or_24_out, and_16_out);
  nand nand_12 (nand_12_out, or_24_out, and_16_out);
  and and_24 (and_24_out, or_24_out, and_16_out);
  or or_18 (or_18_out, or_25_out, and_17_out);
  nand nand_13 (nand_13_out, or_25_out, and_17_out);
  and and_25 (and_25_out, or_25_out, and_17_out);
  or or_19 (or_19_out, or_26_out, and_18_out);
  nand nand_14 (nand_14_out, or_26_out, and_18_out);
  and and_26 (and_26_out, or_26_out, and_18_out);
  or or_20 (or_20_out, or_27_out, and_19_out);
  nand nand_15 (nand_15_out, or_27_out, and_19_out);
  and and_27 (and_27_out, or_27_out, and_19_out);
  or or_21 (or_21_out, or_28_out, and_20_out);
  and and_28 (and_28_out, or_28_out, and_20_out);
  D_Flip_Flop d_ff_2 (.D(or_12_out), .clk(Clock), .Q(Flag010));  // open: Qn, preset, reset
  and and_29 (and_29_out[0], or_14_out, nand_9_out);
  or or_22 (or_22_out, and_5_out, and_21_out);
  and and_30 (and_29_out[1], or_15_out, nand_10_out);
  or or_23 (or_23_out, and_22_out, and_6_out);
  and and_31 (and_29_out[2], or_16_out, nand_11_out);
  or or_24 (or_24_out, and_23_out, and_7_out);
  and and_32 (and_29_out[3], or_17_out, nand_12_out);
  or or_25 (or_25_out, and_24_out, and_8_out);
  and and_33 (and_29_out[4], or_18_out, nand_13_out);
  or or_26 (or_26_out, and_25_out, and_9_out);
  and and_34 (and_29_out[5], or_19_out, nand_14_out);
  or or_27 (or_27_out, and_26_out, and_10_out);
  and and_35 (and_29_out[6], or_20_out, nand_15_out);
  or or_28 (or_28_out, and_27_out, and_11_out);
  and and_36 (and_29_out[7], or_21_out, nand_16_out);
  nand nand_16 (nand_16_out, or_28_out, and_20_out);
  or or_29 (or_29_out, and_28_out, and_12_out);
  // NAND_Gate nand_17 is placed but not wired
  D_Flip_Flop d_ff_3 (.D(or_30_out), .clk(Clock), .Q(Flag000));  // open: Qn, preset, reset
  xor xor_2 (Overflow, or_28_out, or_29_out);
  xor xor_3 (xor_3_out[0], Choose010, Bin[0]);
  xor xor_4 (xor_3_out[1], Choose010, Bin[1]);
  xor xor_5 (xor_3_out[2], Choose010, Bin[2]);
  xor xor_6 (xor_3_out[3], Choose010, Bin[3]);
  xor xor_7 (xor_3_out[4], Choose010, Bin[4]);
  xor xor_8 (xor_3_out[5], Choose010, Bin[5]);
  xor xor_9 (xor_3_out[6], Choose010, Bin[6]);
  xor xor_10 (xor_3_out[7], Choose010, Bin[7]);
  assign not_5_out = ~and_29_out;  // NOT_Gate not_5, 8 bits wide
  not not_6 (not_6_out, Choose100);
  assign controlled_buffer_2_out = not_6_out ? and_29_out : 8'bz;  // Controlled_Buffer controlled_buffer_2
  or or_30 (or_30_out, or_29_out, xor_3_out[7]);
  and and_37 (and_37_out[0], Ain[0], Bin[0]);
  and and_38 (and_37_out[1], Ain[1], Bin[1]);
  and and_39 (and_37_out[2], Ain[2], Bin[2]);
  and and_40 (and_37_out[3], Ain[3], Bin[3]);
  and and_41 (and_37_out[4], Ain[4], Bin[4]);
  and and_42 (and_37_out[5], Ain[5], Bin[5]);
  and and_43 (and_37_out[6], Ain[6], Bin[6]);
  and and_44 (and_37_out[7], Ain[7], Bin[7]);
  D_Flip_Flop d_ff_4 (.D(controlled_buffer_2_out[0]), .clk(Clock), .Q(d_ff_4_q[0]));  // open: Qn, preset, reset
  assign out_14 = and_47_out ? and_37_out : 8'bz;  // Controlled_Buffer controlled_buffer_3
  D_Flip_Flop d_ff_5 (.D(controlled_buffer_2_out[1]), .clk(Clock), .Q(d_ff_4_q[1]));  // open: Qn, preset, reset
  xor xor_11 (xor_11_out[0], Ain[0], Bin[0]);
  xor xor_12 (xor_11_out[1], Ain[1], Bin[1]);
  xor xor_13 (xor_11_out[2], Ain[2], Bin[2]);
  xor xor_14 (xor_11_out[3], Ain[3], Bin[3]);
  xor xor_15 (xor_11_out[4], Ain[4], Bin[4]);
  xor xor_16 (xor_11_out[5], Ain[5], Bin[5]);
  xor xor_17 (xor_11_out[6], Ain[6], Bin[6]);
  xor xor_18 (xor_11_out[7], Ain[7], Bin[7]);
  D_Flip_Flop d_ff_6 (.D(controlled_buffer_2_out[2]), .clk(Clock), .Q(d_ff_4_q[2]));  // open: Qn, preset, reset
  assign out_14 = and_46_out ? xor_11_out : 8'bz;  // Controlled_Buffer controlled_buffer_4
  assign controlled_buffer_2_out = Choose100 ? out_14 : 8'bz;  // Controlled_Buffer controlled_buffer_5
  or or_31 (or_31_out[0], Ain[0], Bin[0]);
  or or_32 (or_31_out[1], Ain[1], Bin[1]);
  or or_33 (or_31_out[2], Ain[2], Bin[2]);
  or or_34 (or_31_out[3], Ain[3], Bin[3]);
  or or_35 (or_31_out[4], Ain[4], Bin[4]);
  or or_36 (or_31_out[5], Ain[5], Bin[5]);
  or or_37 (or_31_out[6], Ain[6], Bin[6]);
  or or_38 (or_31_out[7], Ain[7], Bin[7]);
  assign out_14 = and_45_out ? or_31_out : 8'bz;  // Controlled_Buffer controlled_buffer_6
  D_Flip_Flop d_ff_7 (.D(controlled_buffer_2_out[3]), .clk(Clock), .Q(d_ff_4_q[3]));  // open: Qn, preset, reset
  D_Flip_Flop d_ff_8 (.D(controlled_buffer_2_out[4]), .clk(Clock), .Q(d_ff_4_q[4]));  // open: Qn, preset, reset
  D_Flip_Flop d_ff_9 (.D(controlled_buffer_2_out[5]), .clk(Clock), .Q(d_ff_4_q[5]));  // open: Qn, preset, reset
  not not_7 (not_7_out, Choose010);
  not not_8 (not_8_out, Choose000);
  D_Flip_Flop d_ff_10 (.D(controlled_buffer_2_out[6]), .clk(Clock), .Q(d_ff_4_q[6]));  // open: Qn, preset, reset
  and and_45 (and_45_out, Choose100, Choose010, not_8_out);
  and and_46 (and_46_out, Choose100, not_7_out, Choose000);
  and and_47 (and_47_out, Choose100, not_7_out, not_8_out);
  D_Flip_Flop d_ff_11 (.D(controlled_buffer_2_out[7]), .clk(Clock), .Q(d_ff_4_q[7]));  // open: Qn, preset, reset
  assign Dataout = Enable ? d_ff_4_q : 8'bz;  // Controlled_Buffer controlled_buffer_7
endmodule

module ALU (
  input  in_1,
  input  in_2,
  input  [7:0] in_3,
  input  [7:0] in_4,
  input  in_5,
  output [7:0] out_6,
  output out_7,
  output out_8,
  output out_9,
  output out_10
);

  wire d_ff_1_q, d_ff_1_qn, undriven, undriven_2, undriven_3, undriven_4;

  // main main_1: pin names not known; wires that end beside it: in_1, in_2, in_3, in_4, in_5, out_6, out_7, out_8, out_9, out_10
  D_Flip_Flop d_ff_1 (
    .D(undriven), .clk(undriven_2), .Q(d_ff_1_q), .Qn(d_ff_1_qn), .preset(undriven_3), .reset(undriven_4));
  D_Flip_Flop d_ff_2 (
    .D(undriven), .clk(undriven_2), .Q(d_ff_1_q), .Qn(d_ff_1_qn), .preset(undriven_3), .reset(undriven_4));
  D_Flip_Flop d_ff_3 ();  // open: D, clk, Q, Qn, preset, reset
endmodule
