// Logisim project ADD_SUB_module.ver.00.circ as structural Verilog: 1 circuit, main circuit main
module main (
  input  in_1,
  input  in_2,
  input  in_3,
  input  [7:0] in_4,
  input  [7:0] in_5,
  output [7:0] out_6,
  output out_7
);

  wire and_1_out, and_2_out, and_3_out, and_4_out, and_5_out, and_6_out, and_7_out, and_8_out, and_9_out,
       and_10_out, and_11_out, and_12_out, and_13_out, and_14_out, and_15_out, and_16_out, and_17_out,
       and_18_out, and_19_out, and_20_out, and_21_out, and_22_out, and_23_out, and_24_out, and_25_out,
       and_33_out, nand_1_out, nand_2_out, nand_3_out, nand_4_out, nand_5_out, nand_6_out, nand_7_out,
       nand_8_out, nand_9_out, nand_10_out, nand_11_out, nand_12_out, nand_13_out, nand_14_out, nand_15_out,
       nand_16_out, not_1_out, or_1_out, or_2_out, or_3_out, or_4_out, or_5_out, or_6_out, or_7_out,
       or_8_out, or_9_out, or_10_out, or_11_out, or_12_out, or_13_out, or_14_out, or_15_out, or_16_out,
       or_17_out, or_18_out, or_19_out, or_20_out, or_21_out, or_22_out, or_23_out, or_24_out, or_25_out,
       xor_1_out;
  wire [7:0] xor_3_out;

  xor xor_1 (xor_1_out, in_1, in_3);
  not not_1 (not_1_out, in_2);
  and and_1 (and_1_out, in_2, xor_1_out);
  and and_2 (and_2_out, not_1_out, in_1);
  or or_1 (or_1_out, in_4[0], xor_3_out[0]);
  nand nand_1 (nand_1_out, in_4[0], xor_3_out[0]);
  and and_3 (and_3_out, in_4[0], xor_3_out[0]);
  or or_2 (or_2_out, in_4[1], xor_3_out[1]);
  nand nand_2 (nand_2_out, in_4[1], xor_3_out[1]);
  and and_4 (and_4_out, in_4[1], xor_3_out[1]);
  or or_3 (or_3_out, in_4[2], xor_3_out[2]);
  nand nand_3 (nand_3_out, in_4[2], xor_3_out[2]);
  and and_5 (and_5_out, in_4[2], xor_3_out[2]);
  or or_4 (or_4_out, in_4[3], xor_3_out[3]);
  nand nand_4 (nand_4_out, in_4[3], xor_3_out[3]);
  and and_6 (and_6_out, in_4[3], xor_3_out[3]);
  or or_5 (or_5_out, in_4[4], xor_3_out[4]);
  nand nand_5 (nand_5_out, in_4[4], xor_3_out[4]);
  and and_7 (and_7_out, in_4[4], xor_3_out[4]);
  or or_6 (or_6_out, in_4[5], xor_3_out[5]);
  nand nand_6 (nand_6_out, in_4[5], xor_3_out[5]);
  and and_8 (and_8_out, in_4[5], xor_3_out[5]);
  or or_7 (or_7_out, in_4[6], xor_3_out[6]);
  nand nand_7 (nand_7_out, in_4[6], xor_3_out[6]);
  and and_9 (and_9_out, in_4[6], xor_3_out[6]);
  or or_8 (or_8_out, in_4[7], xor_3_out[7]);
  nand nand_8 (nand_8_out, in_4[7], xor_3_out[7]);
  and and_10 (and_10_out, in_4[7], xor_3_out[7]);
  or or_9 (or_9_out, and_1_out, and_2_out);
  and and_11 (and_11_out, or_1_out, nand_1_out);
  and and_12 (and_12_out, or_2_out, nand_2_out);
  and and_13 (and_13_out, or_3_out, nand_3_out);
  and and_14 (and_14_out, or_4_out, nand_4_out);
  and and_15 (and_15_out, or_5_out, nand_5_out);
  and and_16 (and_16_out, or_6_out, nand_6_out);
  and and_17 (and_17_out, or_7_out, nand_7_out);
  and and_18 (and_18_out, or_8_out, nand_8_out);
  or or_10 (or_10_out, and_11_out, or_9_out);
  nand nand_9 (nand_9_out, and_11_out, or_9_out);
  and and_19 (and_19_out, and_11_out, or_9_out);
  or or_11 (or_11_out, or_17_out, and_12_out);
  nand nand_10 (nand_10_out, or_17_out, and_12_out);
  and and_20 (and_20_out, or_17_out, and_12_out);
  or or_12 (or_12_out, or_18_out, and_13_out);
  nand nand_11 (nand_11_out, or_18_out, and_13_out);
  and and_21 (and_21_out, or_18_out, and_13_out);
  or or_13 (or_13_out, or_19_out, and_14_out);
  nand nand_12 (nand_12_out, or_19_out, and_14_out);
  and and_22 (and_22_out, or_19_out, and_14_out);
  or or_14 (or_14_out, or_20_out, and_15_out);
  nand nand_13 (nand_13_out, or_20_out, and_15_out);
  and and_23 (and_23_out, or_20_out, and_15_out);
  or or_15 (or_15_out, or_21_out, and_16_out);
  nand nand_14 (nand_14_out, or_21_out, and_16_out);
  and and_24 (and_24_out, or_21_out, and_16_out);
  or or_16 (or_16_out, or_22_out, and_17_out);
  and and_25 (and_25_out, or_22_out, and_17_out);
  and and_26 (out_6[0], or_10_out, nand_9_out);
  or or_17 (or_17_out, and_3_out, and_19_out);
  and and_27 (out_6[1], or_11_out, nand_10_out);
  or or_18 (or_18_out, and_20_out, and_4_out);
  and and_28 (out_6[2], or_12_out, nand_11_out);
  or or_19 (or_19_out, and_21_out, and_5_out);
  and and_29 (out_6[3], or_13_out, nand_12_out);
  or or_20 (or_20_out, and_22_out, and_6_out);
  and and_30 (out_6[4], or_14_out, nand_13_out);
  or or_21 (or_21_out, and_23_out, and_7_out);
  and and_31 (out_6[5], or_15_out, nand_14_out);
  or or_22 (or_22_out, and_24_out, and_8_out);
  and and_32 (out_6[6], or_16_out, nand_15_out);
  nand nand_15 (nand_15_out, or_22_out, and_17_out);
  or or_23 (or_23_out, and_25_out, and_9_out);
  or or_24 (or_24_out, or_23_out, and_18_out);
  nand nand_16 (nand_16_out, or_23_out, and_18_out);
  and and_33 (and_33_out, or_23_out, and_18_out);
  and and_34 (out_6[7], or_24_out, nand_16_out);
  or or_25 (or_25_out, and_33_out, and_10_out);
  xor xor_2 (out_7, or_25_out, in_1);
  xor xor_3 (xor_3_out[0], in_1, in_5[0]);
  xor xor_4 (xor_3_out[1], in_1, in_5[1]);
  xor xor_5 (xor_3_out[2], in_1, in_5[2]);
  xor xor_6 (xor_3_out[3], in_1, in_5[3]);
  xor xor_7 (xor_3_out[4], in_1, in_5[4]);
  xor xor_8 (xor_3_out[5], in_1, in_5[5]);
  xor xor_9 (xor_3_out[6], in_1, in_5[6]);
  xor xor_10 (xor_3_out[7], in_1, in_5[7]);
endmodule
