// Logisim project 8_adder_ver_01.circ as structural Verilog: 1 circuit, main circuit main
module main (
  input  [7:0] in_1,
  input  [7:0] in_2,
  output [7:0] out_3,
  output out_4
);

  wire and_1_out, and_2_out, and_3_out, and_4_out, and_5_out, and_6_out, and_8_out, and_9_out, and_10_out,
       and_11_out, and_12_out, and_13_out, and_14_out, and_15_out, and_16_out, and_17_out, and_18_out,
       and_19_out, and_23_out, and_24_out, and_25_out, and_26_out, nand_1_out, nand_2_out, nand_3_out,
       nand_4_out, nand_5_out, nand_6_out, nand_7_out, nand_8_out, nand_9_out, nand_10_out, nand_11_out,
       nand_12_out, nand_13_out, nand_14_out, nand_15_out, or_1_out, or_2_out, or_3_out, or_4_out, or_5_out,
       or_6_out, or_7_out, or_8_out, or_9_out, or_10_out, or_11_out, or_12_out, or_13_out, or_14_out,
       or_15_out, or_16_out, or_17_out, or_18_out, or_19_out, or_20_out, or_21_out;

  or or_1 (or_1_out, in_1[0], in_2[0]);
  nand nand_1 (nand_1_out, in_1[0], in_2[0]);
  and and_1 (and_1_out, in_1[0], in_2[0]);
  or or_2 (or_2_out, in_1[1], in_2[1]);
  nand nand_2 (nand_2_out, in_1[1], in_2[1]);
  and and_2 (and_2_out, in_1[1], in_2[1]);
  or or_3 (or_3_out, in_1[2], in_2[2]);
  nand nand_3 (nand_3_out, in_1[2], in_2[2]);
  and and_3 (and_3_out, in_1[2], in_2[2]);
  or or_4 (or_4_out, in_1[3], in_2[3]);
  nand nand_4 (nand_4_out, in_1[3], in_2[3]);
  and and_4 (and_4_out, in_1[3], in_2[3]);
  or or_5 (or_5_out, in_1[4], in_2[4]);
  nand nand_5 (nand_5_out, in_1[4], in_2[4]);
  and and_5 (and_5_out, in_1[4], in_2[4]);
  or or_6 (or_6_out, in_1[5], in_2[5]);
  nand nand_6 (nand_6_out, in_1[5], in_2[5]);
  and and_6 (and_6_out, in_1[5], in_2[5]);
  and and_7 (out_3[0], or_1_out, nand_1_out);
  and and_8 (and_8_out, or_2_out, nand_2_out);
  and and_9 (and_9_out, or_3_out, nand_3_out);
  and and_10 (and_10_out, or_4_out, nand_4_out);
  and and_11 (and_11_out, or_5_out, nand_5_out);
  or or_7 (or_7_out, in_1[6], in_2[6]);
  nand nand_7 (nand_7_out, in_1[6], in_2[6]);
  and and_12 (and_12_out, in_1[6], in_2[6]);
  or or_8 (or_8_out, in_1[7], in_2[7]);
  nand nand_8 (nand_8_out, in_1[7], in_2[7]);
  and and_13 (and_13_out, in_1[7], in_2[7]);
  or or_9 (or_9_out, and_1_out, and_8_out);
  and and_14 (and_14_out, and_1_out, and_8_out);
  or or_10 (or_10_out, or_12_out, and_9_out);
  and and_15 (and_15_out, or_12_out, and_9_out);
  or or_11 (or_11_out, or_13_out, and_10_out);
  and and_16 (and_16_out, or_13_out, and_10_out);
  and and_17 (and_17_out, or_6_out, nand_6_out);
  and and_18 (and_18_out, or_7_out, nand_7_out);
  and and_19 (and_19_out, or_8_out, nand_8_out);
  and and_20 (out_3[1], or_9_out, nand_9_out);
  nand nand_9 (nand_9_out, and_1_out, and_8_out);
  or or_12 (or_12_out, and_14_out, and_2_out);
  and and_21 (out_3[2], or_10_out, nand_10_out);
  nand nand_10 (nand_10_out, or_12_out, and_9_out);
  or or_13 (or_13_out, and_15_out, and_3_out);
  and and_22 (out_3[3], or_11_out, nand_11_out);
  nand nand_11 (nand_11_out, or_13_out, and_10_out);
  or or_14 (or_14_out, and_16_out, and_4_out);
  or or_15 (or_15_out, or_14_out, and_11_out);
  nand nand_12 (nand_12_out, or_14_out, and_11_out);
  and and_23 (and_23_out, or_14_out, and_11_out);
  or or_16 (or_16_out, or_19_out, and_17_out);
  nand nand_13 (nand_13_out, or_19_out, and_17_out);
  and and_24 (and_24_out, or_19_out, and_17_out);
  or or_17 (or_17_out, or_20_out, and_18_out);
  nand nand_14 (nand_14_out, or_20_out, and_18_out);
  and and_25 (and_25_out, or_20_out, and_18_out);
  or or_18 (or_18_out, or_21_out, and_19_out);
  nand nand_15 (nand_15_out, or_21_out, and_19_out);
  and and_26 (and_26_out, or_21_out, and_19_out);
  and and_27 (out_3[4], or_15_out, nand_12_out);
  or or_19 (or_19_out, and_23_out, and_5_out);
  and and_28 (out_3[5], or_16_out, nand_13_out);
  or or_20 (or_20_out, and_24_out, and_6_out);
  and and_29 (out_3[6], or_17_out, nand_14_out);
  or or_21 (or_21_out, and_25_out, and_12_out);
  and and_30 (out_3[7], or_18_out, nand_15_out);
  or or_22 (out_4, and_26_out, and_13_out);
endmodule
