// Logisim project CPUver.00.circ as structural Verilog: 8 circuits, main circuit main
module Program_counter (
  input  [7:0] Addr_in,
  input  Jmp,
  input  [7:0] addr_pls,
  input  clk,
  output [7:0] Addr_out
);

  wire and_1_out, and_2_out, and_3_out, and_4_out, and_5_out, and_6_out, and_7_out, and_8_out, and_9_out,
       and_10_out, and_11_out, and_12_out, and_13_out, and_14_out, and_15_out, and_16_out, and_17_out,
       and_18_out, and_19_out, and_20_out, and_21_out, and_22_out, and_23_out, and_24_out, and_25_out,
       and_26_out, and_27_out, and_28_out, nand_1_out, nand_2_out, nand_3_out, nand_4_out, nand_5_out,
       nand_6_out, nand_7_out, nand_8_out, nand_9_out, nand_10_out, nand_11_out, nand_12_out, nand_13_out,
       nand_14_out, nand_15_out, not_1_out, or_1_out, or_2_out, or_3_out, or_4_out, or_5_out, or_6_out,
       or_7_out, or_8_out, or_9_out, or_10_out, or_11_out, or_12_out, or_13_out, or_14_out, or_15_out,
       or_16_out, or_17_out, or_18_out, or_19_out, or_20_out, or_21_out;
  wire [7:0] controlled_buffer_1_out, d_ff_9_q;

  assign controlled_buffer_1_out = Jmp ? Addr_in : 8'bz;  // Controlled_Buffer controlled_buffer_1
  assign controlled_buffer_1_out = not_1_out ? d_ff_9_q : 8'bz;  // Controlled_Buffer controlled_buffer_2
  not not_1 (not_1_out, Jmp);
  or or_1 (or_1_out, controlled_buffer_1_out[0], addr_pls[0]);
  nand nand_1 (nand_1_out, controlled_buffer_1_out[0], addr_pls[0]);
  and and_1 (and_1_out, controlled_buffer_1_out[0], addr_pls[0]);
  or or_2 (or_2_out, controlled_buffer_1_out[1], addr_pls[1]);
  nand nand_2 (nand_2_out, controlled_buffer_1_out[1], addr_pls[1]);
  and and_2 (and_2_out, controlled_buffer_1_out[1], addr_pls[1]);
  or or_3 (or_3_out, controlled_buffer_1_out[2], addr_pls[2]);
  nand nand_3 (nand_3_out, controlled_buffer_1_out[2], addr_pls[2]);
  and and_3 (and_3_out, controlled_buffer_1_out[2], addr_pls[2]);
  or or_4 (or_4_out, controlled_buffer_1_out[3], addr_pls[3]);
  nand nand_4 (nand_4_out, controlled_buffer_1_out[3], addr_pls[3]);
  and and_4 (and_4_out, controlled_buffer_1_out[3], addr_pls[3]);
  or or_5 (or_5_out, controlled_buffer_1_out[4], addr_pls[4]);
  nand nand_5 (nand_5_out, controlled_buffer_1_out[4], addr_pls[4]);
  and and_5 (and_5_out, controlled_buffer_1_out[4], addr_pls[4]);
  or or_6 (or_6_out, controlled_buffer_1_out[5], addr_pls[5]);
  nand nand_6 (nand_6_out, controlled_buffer_1_out[5], addr_pls[5]);
  and and_6 (and_6_out, controlled_buffer_1_out[5], addr_pls[5]);
  and and_7 (and_7_out, or_1_out, nand_1_out);
  and and_8 (and_8_out, or_2_out, nand_2_out);
  and and_9 (and_9_out, or_3_out, nand_3_out);
  and and_10 (and_10_out, or_4_out, nand_4_out);
  and and_11 (and_11_out, or_5_out, nand_5_out);
  or or_7 (or_7_out, controlled_buffer_1_out[6], addr_pls[6]);
  nand nand_7 (nand_7_out, controlled_buffer_1_out[6], addr_pls[6]);
  and and_12 (and_12_out, controlled_buffer_1_out[6], addr_pls[6]);
  or or_8 (or_8_out, controlled_buffer_1_out[7], addr_pls[7]);
  nand nand_8 (nand_8_out, controlled_buffer_1_out[7], addr_pls[7]);
  or or_9 (or_9_out, and_1_out, and_8_out);
  and and_13 (and_13_out, and_1_out, and_8_out);
  or or_10 (or_10_out, or_12_out, and_9_out);
  and and_14 (and_14_out, or_12_out, and_9_out);
  or or_11 (or_11_out, or_13_out, and_10_out);
  and and_15 (and_15_out, or_13_out, and_10_out);
  and and_16 (and_16_out, or_6_out, nand_6_out);
  and and_17 (and_17_out, or_7_out, nand_7_out);
  and and_18 (and_18_out, or_8_out, nand_8_out);
  and and_19 (and_19_out, or_9_out, nand_9_out);
  nand nand_9 (nand_9_out, and_1_out, and_8_out);
  or or_12 (or_12_out, and_13_out, and_2_out);
  and and_20 (and_20_out, or_10_out, nand_10_out);
  nand nand_10 (nand_10_out, or_12_out, and_9_out);
  or or_13 (or_13_out, and_14_out, and_3_out);
  and and_21 (and_21_out, or_11_out, nand_11_out);
  nand nand_11 (nand_11_out, or_13_out, and_10_out);
  or or_14 (or_14_out, and_15_out, and_4_out);
  or or_15 (or_15_out, or_14_out, and_11_out);
  nand nand_12 (nand_12_out, or_14_out, and_11_out);
  and and_22 (and_22_out, or_14_out, and_11_out);
  or or_16 (or_16_out, or_19_out, and_16_out);
  nand nand_13 (nand_13_out, or_19_out, and_16_out);
  and and_23 (and_23_out, or_19_out, and_16_out);
  or or_17 (or_17_out, or_20_out, and_17_out);
  nand nand_14 (nand_14_out, or_20_out, and_17_out);
  and and_24 (and_24_out, or_20_out, and_17_out);
  or or_18 (or_18_out, or_21_out, and_18_out);
  nand nand_15 (nand_15_out, or_21_out, and_18_out);
  and and_25 (and_25_out, or_15_out, nand_12_out);
  or or_19 (or_19_out, and_22_out, and_5_out);
  and and_26 (and_26_out, or_16_out, nand_13_out);
  or or_20 (or_20_out, and_23_out, and_6_out);
  and and_27 (and_27_out, or_17_out, nand_14_out);
  or or_21 (or_21_out, and_24_out, and_12_out);
  and and_28 (and_28_out, or_18_out, nand_15_out);
  D_Flip_Flop d_ff_1 (.D(controlled_buffer_1_out[0]), .clk(clk), .Q(Addr_out[0]));  // open: Qn, preset, reset
  D_Flip_Flop d_ff_2 (.D(controlled_buffer_1_out[1]), .clk(clk), .Q(Addr_out[1]));  // open: Qn, preset, reset
  D_Flip_Flop d_ff_3 (.D(controlled_buffer_1_out[2]), .clk(clk), .Q(Addr_out[2]));  // open: Qn, preset, reset
  D_Flip_Flop d_ff_4 (.D(controlled_buffer_1_out[3]), .clk(clk), .Q(Addr_out[3]));  // open: Qn, preset, reset
  D_Flip_Flop d_ff_5 (.D(controlled_buffer_1_out[4]), .clk(clk), .Q(Addr_out[4]));  // open: Qn, preset, reset
  D_Flip_Flop d_ff_6 (.D(controlled_buffer_1_out[5]), .clk(clk), .Q(Addr_out[5]));  // open: Qn, preset, reset
  D_Flip_Flop d_ff_7 (.D(controlled_buffer_1_out[6]), .clk(clk), .Q(Addr_out[6]));  // open: Qn, preset, reset
  D_Flip_Flop d_ff_8 (.D(controlled_buffer_1_out[7]), .clk(clk), .Q(Addr_out[7]));  // open: Qn, preset, reset
  D_Flip_Flop d_ff_9 (.D(and_7_out), .clk(clk), .Q(d_ff_9_q[0]));  // open: Qn, preset, reset
  D_Flip_Flop d_ff_10 (.D(and_19_out), .clk(clk), .Q(d_ff_9_q[1]));  // open: Qn, preset, reset
  D_Flip_Flop d_ff_11 (.D(and_20_out), .clk(clk), .Q(d_ff_9_q[2]));  // open: Qn, preset, reset
  D_Flip_Flop d_ff_12 (.D(and_21_out), .clk(clk), .Q(d_ff_9_q[3]));  // open: Qn, preset, reset
  D_Flip_Flop d_ff_13 (.D(and_25_out), .clk(clk), .Q(d_ff_9_q[4]));  // open: Qn, preset, reset
  D_Flip_Flop d_ff_14 (.D(and_26_out), .clk(clk), .Q(d_ff_9_q[5]));  // open: Qn, preset, reset
  D_Flip_Flop d_ff_15 (.D(and_27_out), .clk(clk), .Q(d_ff_9_q[6]));  // open: Qn, preset, reset
  D_Flip_Flop d_ff_16 (.D(and_28_out), .clk(clk), .Q(d_ff_9_q[7]));  // open: Qn, preset, reset
endmodule

module main (
  input  [7:0] in_1,
  input  in_2,
  input  [7:0] in_3,
  input  in_4,
  input  [15:0] in_5,
  output [7:0] out_6,
  output [7:0] out_7,
  output [7:0] out_8,
  output [2:0] out_9,
  output [7:0] out_10,
  output [2:0] out_11,
  output [15:0] out_12,
  output [7:0] out_13,
  output [15:0] out_14
);

  wire instruction_file_1_alu_enable, instruction_file_1_aluflag_000, instruction_file_1_aluflag_010,
       instruction_file_1_writereg_enable;

  Program_counter program_counter_1 (.Addr_in(in_3), .Jmp(in_4), .addr_pls(in_1), .clk(in_2), .Addr_out(out_8));
  ROM #(.dataWidth(16)) rom_1 (.addr(out_8), .data(out_12));
  ALU alu_1 (
    .Enable(instruction_file_1_alu_enable), .Clock(in_2), .Choose000(instruction_file_1_aluflag_000),
    .Choose010(instruction_file_1_aluflag_010), .Ain(out_7), .Bin(out_10), .Dataout(out_13));  // open: Choose100, Carryout, Carry, Sign, Zero, Overflow, out_14
  Register_file register_file_1 (
    .read_reg1(out_9), .read_reg2(out_11), .write_data(out_6), .ALU_in(out_13),
    .Write_from_ALU(instruction_file_1_alu_enable), .clk(in_2),
    .write_enable(instruction_file_1_writereg_enable), .write_reg(out_9), .read_data1(out_7),
    .read_data2(out_10));
  Instruction_file instruction_file_1 (
    .inst(out_12), .clk(in_2), .read_data_reg(out_10), .write_data(out_6), .read_reg(out_9),
    .read_reg2(out_11), .writereg_enable(instruction_file_1_writereg_enable),
    .ALU_enable(instruction_file_1_alu_enable), .Aluflag_000(instruction_file_1_aluflag_000),
    .Aluflag_010(instruction_file_1_aluflag_010));  // open: INC, DEC

  assign out_14 = out_12;

  // Notes on the sheet:
  //   contents of rom_1 (hex, n*v repeats v):
  //   0 1202 1404 3240
endmodule

module ALU (
  input  Enable,
  input  Clock,
  input  Choose000,
  input  Choose100,
  input  Choose010,
  input  [7:0] Ain,
  input  [7:0] Bin,
  input  Carryout,
  output [7:0] Dataout,
  output Carry,
  output Sign,
  output Zero,
  output Overflow,
  output [7:0] out_14
);

  wire and_1_out, and_2_out, and_3_out, and_4_out, and_5_out, and_6_out, and_7_out, and_8_out, and_9_out,
       and_10_out, and_11_out, and_12_out, and_13_out, and_14_out, and_15_out, and_16_out, and_17_out,
       and_18_out, and_19_out, and_20_out, and_21_out, and_22_out, and_23_out, and_24_out, and_25_out,
       and_26_out, and_27_out, and_28_out, and_45_out, and_46_out, and_47_out, controlled_buffer_1_out,
       nand_1_out, nand_2_out, nand_3_out, nand_4_out, nand_5_out, nand_6_out, nand_7_out, nand_8_out,
       nand_9_out, nand_10_out, nand_11_out, nand_12_out, nand_13_out, nand_14_out, nand_15_out, nand_16_out,
       not_1_out, not_2_out, not_3_out, not_4_out, not_6_out, not_7_out, not_8_out, or_1_out, or_2_out,
       or_3_out, or_4_out, or_5_out, or_6_out, or_7_out, or_8_out, or_9_out, or_10_out, or_11_out, or_12_out,
       or_13_out, or_14_out, or_15_out, or_16_out, or_17_out, or_18_out, or_19_out, or_20_out, or_21_out,
       or_22_out, or_23_out, or_24_out, or_25_out, or_26_out, or_27_out, or_28_out, or_29_out, or_30_out,
       xor_1_out;
  wire [7:0] and_29_out, and_37_out, d_ff_4_q, not_5_out, or_31_out, xor_3_out, xor_11_out;

  not not_1 (not_1_out, Choose100);
  and and_1 (and_1_out, or_1_out, or_2_out, or_3_out);
  or or_1 (or_1_out, not_1_out, Choose100);
  not not_2 (not_2_out, Choose010);
  xor xor_1 (xor_1_out, Choose010, Carryout);
  or or_2 (or_2_out, not_2_out, Choose010);
  or or_3 (or_3_out, not_3_out, Choose000);
  not not_3 (not_3_out, Choose000);
  not not_4 (not_4_out, Choose000);
  and and_2 (and_2_out, Choose000, xor_1_out);
  and and_3 (and_3_out, not_4_out, Choose010);
  and and_4 (and_4_out, not_5_out[0], not_5_out[1], not_5_out[2], not_5_out[3], not_5_out[4], not_5_out[5], not_5_out[6], not_5_out[7]);
  or or_4 (or_4_out, Ain[0], xor_3_out[0]);
  and and_5 (and_5_out, Ain[0], xor_3_out[0]);
  or or_5 (or_5_out, Ain[1], xor_3_out[1]);
  and and_6 (and_6_out, Ain[1], xor_3_out[1]);
  or or_6 (or_6_out, Ain[2], xor_3_out[2]);
  and and_7 (and_7_out, Ain[2], xor_3_out[2]);
  or or_7 (or_7_out, Ain[3], xor_3_out[3]);
  and and_8 (and_8_out, Ain[3], xor_3_out[3]);
  assign controlled_buffer_1_out = and_1_out ? and_4_out : 1'bz;  // Controlled_Buffer controlled_buffer_1
  nand nand_1 (nand_1_out, Ain[0], xor_3_out[0]);
  nand nand_2 (nand_2_out, Ain[1], xor_3_out[1]);
  nand nand_3 (nand_3_out, Ain[2], xor_3_out[2]);
  nand nand_4 (nand_4_out, Ain[3], xor_3_out[3]);
  or or_8 (or_8_out, Ain[4], xor_3_out[4]);
  nand nand_5 (nand_5_out, Ain[4], xor_3_out[4]);
  and and_9 (and_9_out, Ain[4], xor_3_out[4]);
  or or_9 (or_9_out, Ain[5], xor_3_out[5]);
  nand nand_6 (nand_6_out, Ain[5], xor_3_out[5]);
  and and_10 (and_10_out, Ain[5], xor_3_out[5]);
  or or_10 (or_10_out, Ain[6], xor_3_out[6]);
  nand nand_7 (nand_7_out, Ain[6], xor_3_out[6]);
  and and_11 (and_11_out, Ain[6], xor_3_out[6]);
  or or_11 (or_11_out, Ain[7], xor_3_out[7]);
  nand nand_8 (nand_8_out, Ain[7], xor_3_out[7]);
  and and_12 (and_12_out, Ain[7], xor_3_out[7]);
  D_Flip_Flop d_ff_1 (.D(and_29_out[7]), .clk(Clock), .Q(Sign));  // open: Qn, preset, reset
  buf or_12 (or_12_out, controlled_buffer_1_out);  // OR_Gate
  or or_13 (or_13_out, and_2_out, and_3_out);
  and and_13 (and_13_out, or_4_out, nand_1_out);
  and and_14 (and_14_out, or_5_out, nand_2_out);
  and and_15 (and_15_out, or_6_out, nand_3_out);
  and and_16 (and_16_out, or_7_out, nand_4_out);
  and and_17 (and_17_out, or_8_out, nand_5_out);
  and and_18 (and_18_out, or_9_out, nand_6_out);
  and and_19 (and_19_out, or_10_out, nand_7_out);
  and and_20 (and_20_out, or_11_out, nand_8_out);
  or or_14 (or_14_out, and_13_out, or_13_out);
  nand nand_9 (nand_9_out, and_13_out, or_13_out);
  and and_21 (and_21_out, and_13_out, or_13_out);
  or or_15 (or_15_out, or_22_out, and_14_out);
  nand nand_10 (nand_10_out, or_22_out, and_14_out);
  and and_22 (and_22_out, or_22_out, and_14_out);
  or or_16 (or_16_out, or_23_out, and_15_out);
  nand nand_11 (nand_11_out, or_23_out, and_15_out);
  and and_23 (and_23_out, or_23_out, and_15_out);
  or or_17 (or_17_out, or_24_out, and_16_out);
  nand nand_12 (nand_12_out, or_24_out, and_16_out);
  and and_24 (and_24_out, or_24_out, and_16_out);
  or or_18 (or_18_out, or_25_out, and_17_out);
  nand nand_13 (nand_13_out, or_25_out, and_17_out);
  and and_25 (and_25_out, or_25_out, and_17_out);
  or or_19 (or_19_out, or_26_out, and_18_out);
  nand nand_14 (nand_14_out, or_26_out, and_18_out);
  and and_26 (and_26_out, or_26_out, and_18_out);
  or or_20 (or_20_out, or_27_out, and_19_out);
  nand nand_15 (nand_15_out, or_27_out, and_19_out);
  and and_27 (and_27_out, or_27_out, and_19_out);
  or or_21 (or_21_out, or_28_out, and_20_out);
  and and_28 (and_28_out, or_28_out, and_20_out);
  D_Flip_Flop d_ff_2 (.D(or_12_out), .clk(Clock), .Q(Zero));  // open: Qn, preset, reset
  and and_29 (and_29_out[0], or_14_out, nand_9_out);
  or or_22 (or_22_out, and_5_out, and_21_out);
  and and_30 (and_29_out[1], or_15_out, nand_10_out);
  or or_23 (or_23_out, and_22_out, and_6_out);
  and and_31 (and_29_out[2], or_16_out, nand_11_out);
  or or_24 (or_24_out, and_23_out, and_7_out);
  and and_32 (and_29_out[3], or_17_out, nand_12_out);
  or or_25 (or_25_out, and_24_out, and_8_out);
  and and_33 (and_29_out[4], or_18_out, nand_13_out);
  or or_26 (or_26_out, and_25_out, and_9_out);
  and and_34 (and_29_out[5], or_19_out, nand_14_out);
  or or_27 (or_27_out, and_26_out, and_10_out);
  and and_35 (and_29_out[6], or_20_out, nand_15_out);
  or or_28 (or_28_out, and_27_out, and_11_out);
  and and_36 (and_29_out[7], or_21_out, nand_16_out);
  nand nand_16 (nand_16_out, or_28_out, and_20_out);
  or or_29 (or_29_out, and_28_out, and_12_out);
  // NAND_Gate nand_17 is placed but not wired
  D_Flip_Flop d_ff_3 (.D(or_30_out), .clk(Clock), .Q(Carry));  // open: Qn, preset, reset
  xor xor_2 (Overflow, or_28_out, or_29_out);
  xor xor_3 (xor_3_out[0], Choose010, Bin[0]);
  xor xor_4 (xor_3_out[1], Choose010, Bin[1]);
  xor xor_5 (xor_3_out[2], Choose010, Bin[2]);
  xor xor_6 (xor_3_out[3], Choose010, Bin[3]);
  xor xor_7 (xor_3_out[4], Choose010, Bin[4]);
  xor xor_8 (xor_3_out[5], Choose010, Bin[5]);
  xor xor_9 (xor_3_out[6], Choose010, Bin[6]);
  xor xor_10 (xor_3_out[7], Choose010, Bin[7]);
  assign not_5_out = ~and_29_out;  // NOT_Gate not_5, 8 bits wide
  not not_6 (not_6_out, Choose100);
  assign out_14 = not_6_out ? and_29_out : 8'bz;  // Controlled_Buffer controlled_buffer_2
  or or_30 (or_30_out, or_29_out, xor_3_out[7]);
  and and_37 (and_37_out[0], Ain[0], Bin[0]);
  and and_38 (and_37_out[1], Ain[1], Bin[1]);
  and and_39 (and_37_out[2], Ain[2], Bin[2]);
  and and_40 (and_37_out[3], Ain[3], Bin[3]);
  and and_41 (and_37_out[4], Ain[4], Bin[4]);
  and and_42 (and_37_out[5], Ain[5], Bin[5]);
  and and_43 (and_37_out[6], Ain[6], Bin[6]);
  and and_44 (and_37_out[7], Ain[7], Bin[7]);
  D_Flip_Flop d_ff_4 (.D(out_14[0]), .clk(Clock), .Q(d_ff_4_q[0]));  // open: Qn, preset, reset
  assign out_14 = and_47_out ? and_37_out : 8'bz;  // Controlled_Buffer controlled_buffer_3
  D_Flip_Flop d_ff_5 (.D(out_14[1]), .clk(Clock), .Q(d_ff_4_q[1]));  // open: Qn, preset, reset
  xor xor_11 (xor_11_out[0], Ain[0], Bin[0]);
  xor xor_12 (xor_11_out[1], Ain[1], Bin[1]);
  xor xor_13 (xor_11_out[2], Ain[2], Bin[2]);
  xor xor_14 (xor_11_out[3], Ain[3], Bin[3]);
  xor xor_15 (xor_11_out[4], Ain[4], Bin[4]);
  xor xor_16 (xor_11_out[5], Ain[5], Bin[5]);
  xor xor_17 (xor_11_out[6], Ain[6], Bin[6]);
  xor xor_18 (xor_11_out[7], Ain[7], Bin[7]);
  D_Flip_Flop d_ff_6 (.D(out_14[2]), .clk(Clock), .Q(d_ff_4_q[2]));  // open: Qn, preset, reset
  assign out_14 = and_46_out ? xor_11_out : 8'bz;  // Controlled_Buffer controlled_buffer_4
  or or_31 (or_31_out[0], Ain[0], Bin[0]);
  or or_32 (or_31_out[1], Ain[1], Bin[1]);
  or or_33 (or_31_out[2], Ain[2], Bin[2]);
  or or_34 (or_31_out[3], Ain[3], Bin[3]);
  or or_35 (or_31_out[4], Ain[4], Bin[4]);
  or or_36 (or_31_out[5], Ain[5], Bin[5]);
  or or_37 (or_31_out[6], Ain[6], Bin[6]);
  or or_38 (or_31_out[7], Ain[7], Bin[7]);
  assign out_14 = and_45_out ? or_31_out : 8'bz;  // Controlled_Buffer controlled_buffer_5
  D_Flip_Flop d_ff_7 (.D(out_14[3]), .clk(Clock), .Q(d_ff_4_q[3]));  // open: Qn, preset, reset
  D_Flip_Flop d_ff_8 (.D(out_14[4]), .clk(Clock), .Q(d_ff_4_q[4]));  // open: Qn, preset, reset
  D_Flip_Flop d_ff_9 (.D(out_14[5]), .clk(Clock), .Q(d_ff_4_q[5]));  // open: Qn, preset, reset
  not not_7 (not_7_out, Choose010);
  not not_8 (not_8_out, Choose000);
  D_Flip_Flop d_ff_10 (.D(out_14[6]), .clk(Clock), .Q(d_ff_4_q[6]));  // open: Qn, preset, reset
  and and_45 (and_45_out, Choose100, Choose010, not_8_out);
  and and_46 (and_46_out, Choose100, not_7_out, Choose000);
  and and_47 (and_47_out, Choose100, not_7_out, not_8_out);
  D_Flip_Flop d_ff_11 (.D(out_14[7]), .clk(Clock), .Q(d_ff_4_q[7]));  // open: Qn, preset, reset
  assign Dataout = Enable ? d_ff_4_q : 8'bz;  // Controlled_Buffer controlled_buffer_6
endmodule

module Register_file (
  input  [2:0] read_reg1,
  input  [2:0] read_reg2,
  input  [7:0] write_data,
  input  [7:0] ALU_in,
  input  Write_from_ALU,
  input  clk,
  input  write_enable,
  input  [2:0] write_reg,
  output [7:0] read_data1,
  output [7:0] read_data2
);

  wire and_1_out, and_2_out, and_3_out, and_4_out, and_5_out, and_6_out, and_7_out, and_8_out, and_9_out,
       and_10_out, and_11_out, and_12_out, and_13_out, and_14_out, and_15_out, and_16_out, and_17_out,
       and_18_out, and_19_out, and_20_out, and_21_out, and_22_out, and_23_out, and_24_out, and_25_out,
       and_26_out, and_27_out, and_28_out, and_29_out, and_30_out, and_31_out, and_32_out, not_1_out,
       not_2_out, not_3_out, not_4_out, not_5_out, not_6_out, not_7_out, not_8_out, not_9_out, not_10_out,
       not_11_out, not_12_out, not_13_out, not_14_out, not_15_out, not_16_out, not_17_out, not_18_out,
       not_19_out, not_20_out, not_21_out, not_22_out, not_23_out, not_24_out, not_25_out, not_26_out,
       not_27_out, not_28_out, not_29_out, not_30_out, not_31_out, not_32_out, not_33_out, not_34_out,
       not_35_out, not_36_out, not_37_out;
  wire [7:0] controlled_buffer_1_out, d_ff_1_q, d_ff_9_q, d_ff_17_q, d_ff_25_q, d_ff_33_q, d_ff_41_q,
       d_ff_49_q, d_ff_57_q;

  not not_1 (not_1_out, read_reg2[2]);
  not not_2 (not_2_out, read_reg2[1]);
  not not_3 (not_3_out, read_reg2[0]);
  not not_4 (not_4_out, read_reg2[2]);
  and and_1 (and_1_out, not_1_out, not_2_out, not_3_out);
  assign controlled_buffer_1_out = not_5_out ? write_data : 8'bz;  // Controlled_Buffer controlled_buffer_1
  assign controlled_buffer_1_out = Write_from_ALU ? ALU_in : 8'bz;  // Controlled_Buffer controlled_buffer_2
  not not_5 (not_5_out, Write_from_ALU);
  not not_6 (not_6_out, write_reg[2]);
  not not_7 (not_7_out, read_reg2[1]);
  not not_8 (not_8_out, read_reg2[2]);
  and and_2 (and_2_out, not_4_out, not_7_out, read_reg2[0]);
  not not_9 (not_9_out, write_reg[1]);
  not not_10 (not_10_out, write_reg[0]);
  not not_11 (not_11_out, write_reg[2]);
  and and_3 (and_3_out, not_6_out, not_9_out, not_10_out);
  not not_12 (not_12_out, read_reg2[0]);
  not not_13 (not_13_out, read_reg2[2]);
  and and_4 (and_4_out, not_8_out, read_reg2[1], not_12_out);
  not not_14 (not_14_out, write_reg[1]);
  not not_15 (not_15_out, write_reg[2]);
  and and_5 (and_5_out, not_11_out, not_14_out, write_reg[0]);
  and and_6 (and_6_out, not_13_out, read_reg2[1], read_reg2[0]);
  not not_16 (not_16_out, write_reg[0]);
  not not_17 (not_17_out, write_reg[2]);
  and and_7 (and_7_out, not_15_out, write_reg[1], not_16_out);
  not not_18 (not_18_out, read_reg2[1]);
  not not_19 (not_19_out, read_reg2[0]);
  and and_8 (and_8_out, read_reg2[2], not_18_out, not_19_out);
  and and_9 (and_9_out, not_17_out, write_reg[1], write_reg[0]);
  not not_20 (not_20_out, read_reg2[1]);
  and and_10 (and_10_out, read_reg2[2], not_20_out, read_reg2[0]);
  not not_21 (not_21_out, write_reg[1]);
  not not_22 (not_22_out, write_reg[0]);
  and and_11 (and_11_out, write_reg[2], not_21_out, not_22_out);
  not not_23 (not_23_out, read_reg2[0]);
  and and_12 (and_12_out, read_reg2[2], read_reg2[1], not_23_out);
  and and_13 (and_13_out, Write_from_ALU, clk, write_enable);
  not not_24 (not_24_out, write_reg[1]);
  and and_14 (and_14_out, write_reg[2], not_24_out, write_reg[0]);
  and and_15 (and_15_out, read_reg2[2], read_reg2[1], read_reg2[0]);
  D_Flip_Flop d_ff_1 (.D(controlled_buffer_1_out[0]), .clk(and_13_out), .Q(d_ff_1_q[0]));  // open: Qn, preset, reset
  D_Flip_Flop d_ff_2 (.D(controlled_buffer_1_out[1]), .clk(and_13_out), .Q(d_ff_1_q[1]));  // open: Qn, preset, reset
  D_Flip_Flop d_ff_3 (.D(controlled_buffer_1_out[2]), .clk(and_13_out), .Q(d_ff_1_q[2]));  // open: Qn, preset, reset
  D_Flip_Flop d_ff_4 (.D(controlled_buffer_1_out[3]), .clk(and_13_out), .Q(d_ff_1_q[3]));  // open: Qn, preset, reset
  D_Flip_Flop d_ff_5 (.D(controlled_buffer_1_out[4]), .clk(and_13_out), .Q(d_ff_1_q[4]));  // open: Qn, preset, reset
  D_Flip_Flop d_ff_6 (.D(controlled_buffer_1_out[5]), .clk(and_13_out), .Q(d_ff_1_q[5]));  // open: Qn, preset, reset
  D_Flip_Flop d_ff_7 (.D(controlled_buffer_1_out[6]), .clk(and_13_out), .Q(d_ff_1_q[6]));  // open: Qn, preset, reset
  D_Flip_Flop d_ff_8 (.D(controlled_buffer_1_out[7]), .clk(and_13_out), .Q(d_ff_1_q[7]));  // open: Qn, preset, reset
  not not_25 (not_25_out, write_reg[0]);
  and and_16 (and_16_out, write_reg[2], write_reg[1], not_25_out);
  and and_17 (and_17_out, write_reg[2], write_reg[1], write_reg[0]);
  assign read_data2 = and_1_out ? d_ff_1_q : 8'bz;  // Controlled_Buffer controlled_buffer_3
  assign read_data1 = and_19_out ? d_ff_1_q : 8'bz;  // Controlled_Buffer controlled_buffer_4
  D_Flip_Flop d_ff_9 (.D(controlled_buffer_1_out[0]), .clk(and_18_out), .Q(d_ff_9_q[0]));  // open: Qn, preset, reset
  D_Flip_Flop d_ff_10 (.D(controlled_buffer_1_out[1]), .clk(and_18_out), .Q(d_ff_9_q[1]));  // open: Qn, preset, reset
  D_Flip_Flop d_ff_11 (.D(controlled_buffer_1_out[2]), .clk(and_18_out), .Q(d_ff_9_q[2]));  // open: Qn, preset, reset
  D_Flip_Flop d_ff_12 (.D(controlled_buffer_1_out[3]), .clk(and_18_out), .Q(d_ff_9_q[3]));  // open: Qn, preset, reset
  D_Flip_Flop d_ff_13 (.D(controlled_buffer_1_out[4]), .clk(and_18_out), .Q(d_ff_9_q[4]));  // open: Qn, preset, reset
  D_Flip_Flop d_ff_14 (.D(controlled_buffer_1_out[5]), .clk(and_18_out), .Q(d_ff_9_q[5]));  // open: Qn, preset, reset
  D_Flip_Flop d_ff_15 (.D(controlled_buffer_1_out[6]), .clk(and_18_out), .Q(d_ff_9_q[6]));  // open: Qn, preset, reset
  D_Flip_Flop d_ff_16 (.D(controlled_buffer_1_out[7]), .clk(and_18_out), .Q(d_ff_9_q[7]));  // open: Qn, preset, reset
  and and_18 (and_18_out, and_5_out, clk, write_enable);
  assign read_data2 = and_2_out ? d_ff_9_q : 8'bz;  // Controlled_Buffer controlled_buffer_5
  not not_26 (not_26_out, read_reg1[2]);
  not not_27 (not_27_out, read_reg1[1]);
  and and_19 (and_19_out, not_26_out, not_27_out, not_28_out);
  assign read_data1 = and_21_out ? d_ff_9_q : 8'bz;  // Controlled_Buffer controlled_buffer_6
  D_Flip_Flop d_ff_17 (.D(controlled_buffer_1_out[0]), .clk(and_20_out), .Q(d_ff_17_q[0]));  // open: Qn, preset, reset
  D_Flip_Flop d_ff_18 (.D(controlled_buffer_1_out[1]), .clk(and_20_out), .Q(d_ff_17_q[1]));  // open: Qn, preset, reset
  D_Flip_Flop d_ff_19 (.D(controlled_buffer_1_out[2]), .clk(and_20_out), .Q(d_ff_17_q[2]));  // open: Qn, preset, reset
  D_Flip_Flop d_ff_20 (.D(controlled_buffer_1_out[3]), .clk(and_20_out), .Q(d_ff_17_q[3]));  // open: Qn, preset, reset
  D_Flip_Flop d_ff_21 (.D(controlled_buffer_1_out[4]), .clk(and_20_out), .Q(d_ff_17_q[4]));  // open: Qn, preset, reset
  D_Flip_Flop d_ff_22 (.D(controlled_buffer_1_out[5]), .clk(and_20_out), .Q(d_ff_17_q[5]));  // open: Qn, preset, reset
  D_Flip_Flop d_ff_23 (.D(controlled_buffer_1_out[6]), .clk(and_20_out), .Q(d_ff_17_q[6]));  // open: Qn, preset, reset
  D_Flip_Flop d_ff_24 (.D(controlled_buffer_1_out[7]), .clk(and_20_out), .Q(d_ff_17_q[7]));  // open: Qn, preset, reset
  and and_20 (and_20_out, and_7_out, clk, write_enable);
  not not_28 (not_28_out, read_reg1[0]);
  not not_29 (not_29_out, read_reg1[2]);
  not not_30 (not_30_out, read_reg1[1]);
  and and_21 (and_21_out, not_29_out, not_30_out, read_reg1[0]);
  and and_22 (and_22_out, and_9_out, clk, write_enable);
  not not_31 (not_31_out, read_reg1[2]);
  and and_23 (and_23_out, not_31_out, read_reg1[1], not_32_out);
  assign read_data1 = and_23_out ? d_ff_17_q : 8'bz;  // Controlled_Buffer controlled_buffer_7
  assign read_data2 = and_4_out ? d_ff_17_q : 8'bz;  // Controlled_Buffer controlled_buffer_8
  D_Flip_Flop d_ff_25 (.D(controlled_buffer_1_out[0]), .clk(and_22_out), .Q(d_ff_25_q[0]));  // open: Qn, preset, reset
  D_Flip_Flop d_ff_26 (.D(controlled_buffer_1_out[1]), .clk(and_22_out), .Q(d_ff_25_q[1]));  // open: Qn, preset, reset
  D_Flip_Flop d_ff_27 (.D(controlled_buffer_1_out[2]), .clk(and_22_out), .Q(d_ff_25_q[2]));  // open: Qn, preset, reset
  D_Flip_Flop d_ff_28 (.D(controlled_buffer_1_out[3]), .clk(and_22_out), .Q(d_ff_25_q[3]));  // open: Qn, preset, reset
  D_Flip_Flop d_ff_29 (.D(controlled_buffer_1_out[4]), .clk(and_22_out), .Q(d_ff_25_q[4]));  // open: Qn, preset, reset
  D_Flip_Flop d_ff_30 (.D(controlled_buffer_1_out[5]), .clk(and_22_out), .Q(d_ff_25_q[5]));  // open: Qn, preset, reset
  D_Flip_Flop d_ff_31 (.D(controlled_buffer_1_out[6]), .clk(and_22_out), .Q(d_ff_25_q[6]));  // open: Qn, preset, reset
  D_Flip_Flop d_ff_32 (.D(controlled_buffer_1_out[7]), .clk(and_22_out), .Q(d_ff_25_q[7]));  // open: Qn, preset, reset
  not not_32 (not_32_out, read_reg1[0]);
  not not_33 (not_33_out, read_reg1[2]);
  and and_24 (and_24_out, not_33_out, read_reg1[1], read_reg1[0]);
  and and_25 (and_25_out, and_11_out, clk, write_enable);
  not not_34 (not_34_out, read_reg1[1]);
  and and_26 (and_26_out, read_reg1[2], not_34_out, not_35_out);
  assign read_data1 = and_24_out ? d_ff_25_q : 8'bz;  // Controlled_Buffer controlled_buffer_9
  assign read_data2 = and_6_out ? d_ff_25_q : 8'bz;  // Controlled_Buffer controlled_buffer_10
  not not_35 (not_35_out, read_reg1[0]);
  not not_36 (not_36_out, read_reg1[1]);
  and and_27 (and_27_out, read_reg1[2], not_36_out, read_reg1[0]);
  D_Flip_Flop d_ff_33 (.D(controlled_buffer_1_out[0]), .clk(and_25_out), .Q(d_ff_33_q[0]));  // open: Qn, preset, reset
  D_Flip_Flop d_ff_34 (.D(controlled_buffer_1_out[1]), .clk(and_25_out), .Q(d_ff_33_q[1]));  // open: Qn, preset, reset
  D_Flip_Flop d_ff_35 (.D(controlled_buffer_1_out[2]), .clk(and_25_out), .Q(d_ff_33_q[2]));  // open: Qn, preset, reset
  D_Flip_Flop d_ff_36 (.D(controlled_buffer_1_out[3]), .clk(and_25_out), .Q(d_ff_33_q[3]));  // open: Qn, preset, reset
  D_Flip_Flop d_ff_37 (.D(controlled_buffer_1_out[4]), .clk(and_25_out), .Q(d_ff_33_q[4]));  // open: Qn, preset, reset
  D_Flip_Flop d_ff_38 (.D(controlled_buffer_1_out[5]), .clk(and_25_out), .Q(d_ff_33_q[5]));  // open: Qn, preset, reset
  D_Flip_Flop d_ff_39 (.D(controlled_buffer_1_out[6]), .clk(and_25_out), .Q(d_ff_33_q[6]));  // open: Qn, preset, reset
  D_Flip_Flop d_ff_40 (.D(controlled_buffer_1_out[7]), .clk(and_25_out), .Q(d_ff_33_q[7]));  // open: Qn, preset, reset
  and and_28 (and_28_out, and_14_out, clk, write_enable);
  and and_29 (and_29_out, read_reg1[2], read_reg1[1], not_37_out);
  assign read_data2 = and_8_out ? d_ff_33_q : 8'bz;  // Controlled_Buffer controlled_buffer_11
  not not_37 (not_37_out, read_reg1[0]);
  and and_30 (and_30_out, read_reg1[2], read_reg1[1], read_reg1[0]);
  assign read_data1 = and_26_out ? d_ff_33_q : 8'bz;  // Controlled_Buffer controlled_buffer_12
  D_Flip_Flop d_ff_41 (.D(controlled_buffer_1_out[0]), .clk(and_28_out), .Q(d_ff_41_q[0]));  // open: Qn, preset, reset
  D_Flip_Flop d_ff_42 (.D(controlled_buffer_1_out[1]), .clk(and_28_out), .Q(d_ff_41_q[1]));  // open: Qn, preset, reset
  D_Flip_Flop d_ff_43 (.D(controlled_buffer_1_out[2]), .clk(and_28_out), .Q(d_ff_41_q[2]));  // open: Qn, preset, reset
  D_Flip_Flop d_ff_44 (.D(controlled_buffer_1_out[3]), .clk(and_28_out), .Q(d_ff_41_q[3]));  // open: Qn, preset, reset
  D_Flip_Flop d_ff_45 (.D(controlled_buffer_1_out[4]), .clk(and_28_out), .Q(d_ff_41_q[4]));  // open: Qn, preset, reset
  D_Flip_Flop d_ff_46 (.D(controlled_buffer_1_out[5]), .clk(and_28_out), .Q(d_ff_41_q[5]));  // open: Qn, preset, reset
  D_Flip_Flop d_ff_47 (.D(controlled_buffer_1_out[6]), .clk(and_28_out), .Q(d_ff_41_q[6]));  // open: Qn, preset, reset
  D_Flip_Flop d_ff_48 (.D(controlled_buffer_1_out[7]), .clk(and_28_out), .Q(d_ff_41_q[7]));  // open: Qn, preset, reset
  and and_31 (and_31_out, and_16_out, clk, write_enable);
  assign read_data1 = and_27_out ? d_ff_41_q : 8'bz;  // Controlled_Buffer controlled_buffer_13
  assign read_data2 = and_10_out ? d_ff_41_q : 8'bz;  // Controlled_Buffer controlled_buffer_14
  D_Flip_Flop d_ff_49 (.D(controlled_buffer_1_out[0]), .clk(and_31_out), .Q(d_ff_49_q[0]));  // open: Qn, preset, reset
  D_Flip_Flop d_ff_50 (.D(controlled_buffer_1_out[1]), .clk(and_31_out), .Q(d_ff_49_q[1]));  // open: Qn, preset, reset
  D_Flip_Flop d_ff_51 (.D(controlled_buffer_1_out[2]), .clk(and_31_out), .Q(d_ff_49_q[2]));  // open: Qn, preset, reset
  D_Flip_Flop d_ff_52 (.D(controlled_buffer_1_out[3]), .clk(and_31_out), .Q(d_ff_49_q[3]));  // open: Qn, preset, reset
  D_Flip_Flop d_ff_53 (.D(controlled_buffer_1_out[4]), .clk(and_31_out), .Q(d_ff_49_q[4]));  // open: Qn, preset, reset
  D_Flip_Flop d_ff_54 (.D(controlled_buffer_1_out[5]), .clk(and_31_out), .Q(d_ff_49_q[5]));  // open: Qn, preset, reset
  D_Flip_Flop d_ff_55 (.D(controlled_buffer_1_out[6]), .clk(and_31_out), .Q(d_ff_49_q[6]));  // open: Qn, preset, reset
  D_Flip_Flop d_ff_56 (.D(controlled_buffer_1_out[7]), .clk(and_31_out), .Q(d_ff_49_q[7]));  // open: Qn, preset, reset
  and and_32 (and_32_out, and_17_out, clk, write_enable);
  assign read_data2 = and_12_out ? d_ff_49_q : 8'bz;  // Controlled_Buffer controlled_buffer_15
  assign read_data1 = and_29_out ? d_ff_49_q : 8'bz;  // Controlled_Buffer controlled_buffer_16
  D_Flip_Flop d_ff_57 (.D(controlled_buffer_1_out[0]), .clk(and_32_out), .Q(d_ff_57_q[0]));  // open: Qn, preset, reset
  D_Flip_Flop d_ff_58 (.D(controlled_buffer_1_out[1]), .clk(and_32_out), .Q(d_ff_57_q[1]));  // open: Qn, preset, reset
  D_Flip_Flop d_ff_59 (.D(controlled_buffer_1_out[2]), .clk(and_32_out), .Q(d_ff_57_q[2]));  // open: Qn, preset, reset
  D_Flip_Flop d_ff_60 (.D(controlled_buffer_1_out[3]), .clk(and_32_out), .Q(d_ff_57_q[3]));  // open: Qn, preset, reset
  D_Flip_Flop d_ff_61 (.D(controlled_buffer_1_out[4]), .clk(and_32_out), .Q(d_ff_57_q[4]));  // open: Qn, preset, reset
  D_Flip_Flop d_ff_62 (.D(controlled_buffer_1_out[5]), .clk(and_32_out), .Q(d_ff_57_q[5]));  // open: Qn, preset, reset
  D_Flip_Flop d_ff_63 (.D(controlled_buffer_1_out[6]), .clk(and_32_out), .Q(d_ff_57_q[6]));  // open: Qn, preset, reset
  D_Flip_Flop d_ff_64 (.D(controlled_buffer_1_out[7]), .clk(and_32_out), .Q(d_ff_57_q[7]));  // open: Qn, preset, reset
  assign read_data1 = and_30_out ? d_ff_57_q : 8'bz;  // Controlled_Buffer controlled_buffer_17
  assign read_data2 = and_15_out ? d_ff_57_q : 8'bz;  // Controlled_Buffer controlled_buffer_18
endmodule

module Instruction_file (
  input  [15:0] inst,
  input  clk,
  input  [7:0] read_data_reg,
  output [7:0] write_data,
  output [2:0] read_reg,
  output [2:0] read_reg2,
  output writereg_enable,
  output ALU_enable,
  output Aluflag_000,
  output Aluflag_010,
  output INC,
  output DEC
);

  wire control_unit_1_flag_100, control_unit_1_writereg_src, not_1_out;
  wire [3:0] instruction_decoder_1_opcode;
  wire [7:0] instruction_decoder_1_some_value_shit;
  wire [15:0] instruction_register_1_inst_reg_out;

  Instruction_register instruction_register_1 (
    .Inst_reg_in(inst), .clk(clk), .inst_reg_out(instruction_register_1_inst_reg_out));
  Instruction_decoder instruction_decoder_1 (
    .inst_in(instruction_register_1_inst_reg_out), .some_value_shit(instruction_decoder_1_some_value_shit),
    .reg1(read_reg), .reg2(read_reg2), .opcode(instruction_decoder_1_opcode));  // open: someflagtypeshit_doesnt_matter
  Control_unit control_unit_1 (
    .opcode(instruction_decoder_1_opcode), .writereg_enable(writereg_enable),
    .writereg_src(control_unit_1_writereg_src), .ALU_enable(ALU_enable), .Flag_000(Aluflag_000),
    .Flag_010(Aluflag_010), .INCREMENT(INC), .Flag_100(control_unit_1_flag_100), .DECREMENT(DEC));
  assign write_data = control_unit_1_writereg_src ? instruction_decoder_1_some_value_shit : 8'bz;  // Controlled_Buffer controlled_buffer_1
  assign write_data = not_1_out ? read_data_reg : 8'bz;  // Controlled_Buffer controlled_buffer_2
  not not_1 (not_1_out, control_unit_1_writereg_src);
endmodule

module Instruction_register (
  input  [15:0] Inst_reg_in,
  input  clk,
  output [15:0] inst_reg_out
);

  D_Flip_Flop d_ff_1 (.D(Inst_reg_in[8]), .clk(clk), .Q(inst_reg_out[8]));  // open: Qn, preset, reset
  D_Flip_Flop d_ff_2 (.D(Inst_reg_in[9]), .clk(clk), .Q(inst_reg_out[9]));  // open: Qn, preset, reset
  D_Flip_Flop d_ff_3 (.D(Inst_reg_in[10]), .clk(clk), .Q(inst_reg_out[10]));  // open: Qn, preset, reset
  D_Flip_Flop d_ff_4 (.D(Inst_reg_in[11]), .clk(clk), .Q(inst_reg_out[11]));  // open: Qn, preset, reset
  D_Flip_Flop d_ff_5 (.D(Inst_reg_in[12]), .clk(clk), .Q(inst_reg_out[12]));  // open: Qn, preset, reset
  D_Flip_Flop d_ff_6 (.D(Inst_reg_in[13]), .clk(clk), .Q(inst_reg_out[13]));  // open: Qn, preset, reset
  D_Flip_Flop d_ff_7 (.D(Inst_reg_in[14]), .clk(clk), .Q(inst_reg_out[14]));  // open: Qn, preset, reset
  D_Flip_Flop d_ff_8 (.D(Inst_reg_in[15]), .clk(clk), .Q(inst_reg_out[15]));  // open: Qn, preset, reset
  D_Flip_Flop d_ff_9 (.D(Inst_reg_in[0]), .clk(clk), .Q(inst_reg_out[0]));  // open: Qn, preset, reset
  D_Flip_Flop d_ff_10 (.D(Inst_reg_in[1]), .clk(clk), .Q(inst_reg_out[1]));  // open: Qn, preset, reset
  D_Flip_Flop d_ff_11 (.D(Inst_reg_in[2]), .clk(clk), .Q(inst_reg_out[2]));  // open: Qn, preset, reset
  D_Flip_Flop d_ff_12 (.D(Inst_reg_in[3]), .clk(clk), .Q(inst_reg_out[3]));  // open: Qn, preset, reset
  D_Flip_Flop d_ff_13 (.D(Inst_reg_in[4]), .clk(clk), .Q(inst_reg_out[4]));  // open: Qn, preset, reset
  D_Flip_Flop d_ff_14 (.D(Inst_reg_in[5]), .clk(clk), .Q(inst_reg_out[5]));  // open: Qn, preset, reset
  D_Flip_Flop d_ff_15 (.D(Inst_reg_in[6]), .clk(clk), .Q(inst_reg_out[6]));  // open: Qn, preset, reset
  D_Flip_Flop d_ff_16 (.D(Inst_reg_in[7]), .clk(clk), .Q(inst_reg_out[7]));  // open: Qn, preset, reset
endmodule

module Instruction_decoder (
  input  [15:0] inst_in,
  output [7:0] some_value_shit,
  output someflagtypeshit_doesnt_matter,
  output [2:0] reg1,
  output [2:0] reg2,
  output [3:0] opcode
);


  assign opcode = inst_in[15:12];
  assign reg1 = inst_in[11:9];
  assign reg2 = inst_in[7:5];
  assign some_value_shit = inst_in[7:0];
  assign someflagtypeshit_doesnt_matter = inst_in[8];
endmodule

module Control_unit (
  input  [3:0] opcode,
  output writereg_enable,
  output writereg_src,
  output ALU_enable,
  output Flag_000,
  output Flag_010,
  output INCREMENT,
  output Flag_100,
  output DECREMENT
);

  wire ADD_out, and_1_out, and_2_out, and_3_out, and_4_out, and_5_out, and_6_out, and_7_out, and_8_out,
       and_9_out, and_10_out, LDI_out, MOV_out, not_1_out, not_2_out, not_3_out, not_4_out, not_5_out,
       not_6_out, not_7_out, not_8_out, not_9_out, not_10_out, not_11_out, not_12_out, not_13_out,
       not_14_out, not_15_out, not_16_out, not_17_out, not_18_out, not_19_out, not_20_out, not_21_out,
       not_22_out, not_23_out, not_24_out, not_25_out, not_26_out, not_27_out, not_28_out, not_29_out,
       not_30_out, not_31_out, not_32_out;

  not not_1 (not_1_out, opcode[0]);
  not not_2 (not_2_out, opcode[1]);
  and and_1 (and_1_out, not_1_out, not_2_out, not_3_out, not_4_out);
  not not_3 (not_3_out, opcode[2]);
  not not_4 (not_4_out, opcode[3]);
  not not_5 (not_5_out, opcode[1]);
  and LDI (LDI_out, opcode[0], not_5_out, not_6_out, not_7_out);
  not not_6 (not_6_out, opcode[2]);
  not not_7 (not_7_out, opcode[3]);
  not not_8 (not_8_out, opcode[0]);
  and MOV (MOV_out, not_8_out, opcode[1], not_9_out, not_10_out);
  not not_9 (not_9_out, opcode[2]);
  not not_10 (not_10_out, opcode[2]);
  and ADD (ADD_out, opcode[0], opcode[1], not_11_out, not_12_out);
  not not_11 (not_11_out, opcode[2]);
  not not_12 (not_12_out, opcode[3]);
  not not_13 (not_13_out, opcode[0]);
  not not_14 (not_14_out, opcode[1]);
  and SUB (Flag_010, not_13_out, not_14_out, opcode[2], not_15_out);
  not not_15 (not_15_out, opcode[3]);
  not not_16 (not_16_out, opcode[1]);
  and INC (INCREMENT, opcode[0], not_16_out, opcode[2], not_17_out);
  not not_17 (not_17_out, opcode[3]);
  not not_18 (not_18_out, opcode[0]);
  and DEC (DECREMENT, not_18_out, opcode[1], opcode[2], not_19_out);
  not not_19 (not_19_out, opcode[3]);
  and and_2 (and_2_out, opcode[0], opcode[1], opcode[2], not_20_out);
  not not_20 (not_20_out, opcode[3]);
  not not_21 (not_21_out, opcode[0]);
  not not_22 (not_22_out, opcode[1]);
  and and_3 (and_3_out, not_21_out, not_22_out, not_23_out, opcode[3]);
  not not_23 (not_23_out, opcode[2]);
  not not_24 (not_24_out, opcode[1]);
  and and_4 (and_4_out, opcode[0], not_24_out, not_25_out, opcode[3]);
  not not_25 (not_25_out, opcode[2]);
  not not_26 (not_26_out, opcode[0]);
  and and_5 (and_5_out, not_26_out, opcode[1], not_27_out, opcode[3]);
  not not_27 (not_27_out, opcode[2]);
  and and_6 (and_6_out, opcode[0], opcode[1], not_28_out, opcode[3]);
  not not_28 (not_28_out, opcode[2]);
  not not_29 (not_29_out, opcode[0]);
  not not_30 (not_30_out, opcode[1]);
  and and_7 (and_7_out, not_29_out, not_30_out, opcode[2], opcode[3]);
  not not_31 (not_31_out, opcode[1]);
  and and_8 (and_8_out, opcode[0], not_31_out, opcode[2], opcode[3]);
  not not_32 (not_32_out, opcode[0]);
  and and_9 (and_9_out, not_32_out, opcode[1], opcode[2], opcode[3]);
  and and_10 (and_10_out, opcode[0], opcode[1], opcode[2], opcode[3]);
  or or_1 (writereg_enable, LDI_out, INCREMENT, DECREMENT, MOV_out);
  buf or_2 (writereg_src, LDI_out);  // OR_Gate
  or or_3 (ALU_enable, INCREMENT, Flag_010, DECREMENT, ADD_out);
endmodule
